# Fritzing sketch cirpyClock (saved by Fritzing 0.9.3b)

parts:
  RP2040 = Adafruit QT Py RP2040 [part_number="Adafruit #4900"]
  DS3231 = Adafruit DS3231 STEMMA QT [part_number="Adafruit #5188"]
  7SEG = Seven-Segment LED Backpack 1.2 Inch Digits [part_number=1270]
  LDR = Photocell (LDR) [package=THT]
  R1 = Resistor [tolerance=±5% resistance=10k package=THT]
  SW1 = DIP SWITCH [package=dipswitch-02]

nets:
  N1: RP2040.A0, LDR.pin_1, R1.Pin_1
  N2: RP2040.SDA, DS3231.SDA, 7SEG.SDA
  N3: RP2040.SCL, DS3231.SCL, 7SEG.SCL
  N4: RP2040.MISO, SW1.1
  N5: RP2040.MOSI, DS3231.SQW
  +3V3: RP2040.+3V3, DS3231.VCC, 7SEG.VDD, LDR.pin_0, SW1.4
  GND: RP2040.GND, DS3231.GND, 7SEG.GND, R1.Pin_0
  N6: RP2040.+5V, 7SEG.VCCIO

custom parts:
  Adafruit QT Py RP2040: Description What a cutie pie! Or is it... a QT Py? This diminutive dev board comes with one of our new favorite chip, the RP2040. It's been made famous in the new Raspberry Pi Pico and our Feather RP2040 and ItsyBitsy RP2040, but what if we wanted something really smol? A new chip means a new QT Py, and the Raspberry Pi RP2040 is no exception. When we saw this chip we thought "this chip is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
  Adafruit DS3231 STEMMA QT: The datasheet for the DS3231 explains that this part is an "Extremely Accurate I²C-Integrated RTC/TCXO/Crystal". And, hey, it does exactly what it says on the tin! This Real Time Clock (RTC) is the most precise you can get in a small, low-power package. We've had a breakout board version of this RTC for a while, but we want to make it even easier for folks to use, so now it comes with STEMMA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
  Seven-Segment LED Backpack 1.2 Inch Digits: This jumbo 1.2" 7-segment LED display includes a driver chip for simple control via an I2C interface. The backpack features address-selection jumpers so you can connect up to eight displays on a single I2C bus.
